// Logisim project logisim.circ as structural Verilog: 7 circuits, main circuit main
module main (
);

  ALU alu_1 ();  // open: Accumulator, Active, Control_Unit, BUS, Carry, Accumulator_2
endmodule

module ALU (
  input  [7:0] Accumulator,
  input  [7:0] BUS,
  input  Active,
  input  [2:0] Control_Unit,
  output Carry,
  output [7:0] Accumulator_2
);

  wire [7:0] Adder_output, Inverter_output, multiplexer_1_out;

  Inverter Inverter (.Input(Accumulator), .Output(Inverter_output));
  Adder Adder (.Sub(Control_Unit[0]), .A(BUS), .B(Accumulator), .Output(Adder_output), .Carry(Carry));
  Multiplexer #(.select(3), .width(8), .enable("false")) multiplexer_1 (
    .in0(Adder_output), .in1(Adder_output), .in7(Inverter_output), .out(multiplexer_1_out), .sel(Control_Unit));  // open: in2, in3, in4, in5, in6
  assign Accumulator_2 = Active ? multiplexer_1_out : 8'bz;  // Controlled_Buffer controlled_buffer_1
endmodule

module Inverter (
  input  [7:0] Input,
  output [7:0] Output
);

  not not_1 (Output[0], Input[0]);
  not not_2 (Output[1], Input[1]);
  not not_3 (Output[2], Input[2]);
  not not_4 (Output[3], Input[3]);
  not not_5 (Output[4], Input[4]);
  not not_6 (Output[5], Input[5]);
  not not_7 (Output[6], Input[6]);
  not not_8 (Output[7], Input[7]);
endmodule

module Adder (
  input  Sub,
  input  [7:0] A,
  input  [7:0] B,
  output [7:0] Output,
  output Carry
);

  wire undriven, undriven_2, undriven_3, undriven_4, undriven_5, undriven_6, undriven_7, undriven_8,
       xor_1_out, xor_2_out, xor_3_out, xor_4_out, xor_5_out, xor_6_out, xor_7_out, xor_8_out;

  xor xor_1 (xor_1_out, B[0], Sub);
  xor xor_2 (xor_2_out, B[1], Sub);
  xor xor_3 (xor_3_out, B[2], Sub);
  xor xor_4 (xor_4_out, B[3], Sub);
  xor xor_5 (xor_5_out, B[4], Sub);
  xor xor_6 (xor_6_out, B[5], Sub);
  xor xor_7 (xor_7_out, B[6], Sub);
  xor xor_8 (xor_8_out, B[7], Sub);
  FullAdder fulladder_1 (.Carry_In(Sub), .A(A[0]), .B(xor_1_out), .Sum(Output[0]), .Carry_Out(undriven));
  FullAdder fulladder_2 (.Carry_In(undriven), .A(A[1]), .B(xor_2_out), .Sum(Output[1]), .Carry_Out(undriven_2));
  FullAdder fulladder_3 (.Carry_In(undriven_2), .A(A[2]), .B(xor_3_out), .Sum(Output[2]), .Carry_Out(undriven_3));
  FullAdder fulladder_4 (.Carry_In(undriven_3), .A(A[3]), .B(xor_4_out), .Sum(Output[3]), .Carry_Out(undriven_4));
  FullAdder fulladder_5 (.Carry_In(undriven_4), .A(A[4]), .B(xor_5_out), .Sum(Output[4]), .Carry_Out(undriven_5));
  FullAdder fulladder_6 (.Carry_In(undriven_5), .A(A[5]), .B(xor_6_out), .Sum(Output[5]), .Carry_Out(undriven_6));
  FullAdder fulladder_7 (.Carry_In(undriven_6), .A(A[6]), .B(xor_7_out), .Sum(Output[6]), .Carry_Out(undriven_7));
  FullAdder fulladder_8 (.Carry_In(undriven_7), .A(A[7]), .B(xor_8_out), .Sum(Output[7]), .Carry_Out(undriven_8));
  xor xor_9 (Carry, undriven_8, Sub);
endmodule

module FullAdder (
  input  Carry_In,
  input  A,
  input  Sum,
  input  B,
  input  Carry_Out
);

  wire undriven, undriven_2, undriven_3;

  HalfAdder halfadder_1 (.A(A), .B(B), .Sum(undriven), .Carry(undriven_2));
  HalfAdder halfadder_2 (.A(Carry_In), .B(undriven), .Sum(Sum), .Carry(undriven_3));
  or or_1 (Carry_Out, undriven_3, undriven_2);
endmodule

module HalfAdder (
  input  A,
  input  Sum,
  input  B,
  input  Carry
);

  xor xor_1 (Sum, A, B);
  and and_1 (Carry, A, B);
endmodule

module Tests (
  output [7:0] out_1,
  output [7:0] out_2,
  output out_3
);

  Inverter inverter_1 (.Input(8'hfe), .Output(out_1));
  Adder adder_1 (.Sub(1'b0), .A(8'h3), .B(8'hc), .Output(out_2), .Carry(out_3));
endmodule
